# Fritzing sketch Diagram (saved by Fritzing 0.9.9b)
breadboards: 3

parts:
  Part1 = Arduino Uno (Rev3) - ICSP
  LED1 = smd LED [color="Red (633nm)" package="0603 [SMD]"]
  LED2 = smd LED [color="Red (633nm)" package="0603 [SMD]"]
  LED3 = smd LED [color="Red (633nm)" package="0603 [SMD]"]
  R1 = Resistor [tolerance=±5% power=0.25 resistance=220 package=THT]
  R2 = Resistor [tolerance=±5% power=0.25 resistance=220 package=THT]
  R3 = Resistor [tolerance=±5% power=0.25 resistance=220 package=THT]
  R4 = Resistor [tolerance=±5% power=0.25 resistance=220 package=THT]
  R5 = Resistor [tolerance=±5% power=0.25 resistance=220 package=THT]
  R6 = Resistor [tolerance=±5% power=0.25 resistance=220 package=THT]
  LED4 = smd LED [color="Red (633nm)" package="0603 [SMD]"]
  LED5 = smd LED [color="Red (633nm)" package="0603 [SMD]"]
  LED6 = smd LED [color="Red (633nm)" package="0603 [SMD]"]
  J1 = Piezo Speaker
  R7 = Resistor [tolerance=±5% resistance=220 package="0805 [SMD]"]
  7_Segment1 = 7 Segment Display
  R8 = Resistor [tolerance=±5% resistance=220 package="0805 [SMD]"]
  R9 = Resistor [tolerance=±5% resistance=220 package="0805 [SMD]"]
  R10 = Resistor [tolerance=±5% power=0.25 resistance=220 package=THT]
  R11 = Resistor [tolerance=±5% power=0.25 resistance=220 package=THT]
  R12 = Resistor [tolerance=±5% power=0.25 resistance=220 package=THT]
  R13 = Resistor [tolerance=±5% power=0.25 resistance=220 package=THT]
  R14 = Resistor [tolerance=±5% power=0.25 resistance=220 package=THT]
  R15 = Resistor [tolerance=±5% power=0.25 resistance=220 package=THT]
  R16 = Resistor [tolerance=±5% power=0.25 resistance=220 package=THT]
  U1 = PCF8574 [package="DIP16 [THT]"]
  R17 = Resistor [tolerance=±5% resistance=220 package="0805 [SMD]"]
  J2 = Basic Servo
  S1 = SWITCH-MOMENTARY-2 [package=tactile_switch_tall]
  S2 = SWITCH-MOMENTARY-2 [package=tactile_switch_tall]
  S3 = SWITCH-MOMENTARY-2 [package=tactile_switch_tall]
  S4 = SWITCH-MOMENTARY-2 [package=tactile_switch_tall]
  R18 = Resistor [tolerance=±5% resistance=220 package="2512 [SMD]"]
  R19 = Resistor [tolerance=±5% resistance=220 package="2512 [SMD]"]
  R20 = Resistor [tolerance=±5% resistance=220 package="2512 [SMD]"]
  R21 = Resistor [tolerance=±5% resistance=220 package="2512 [SMD]"]

nets:
  N1: Part1.A1, R7.Pin_0
  N2: Part1.D8, R5.Pin_1, LED5.anode
  N3: Part1.D9_PWM, U1.P5
  N4: Part1.D10_PWM/SS, R6.Pin_1, LED6.anode
  N5: Part1.D11_PWM/MOSI, U1.P6
  N6: Part1.D12/MISO, U1.INT
  N7: Part1.D13/SCK, J2.vcc
  N8: Part1.D2, R1.Pin_1
  N9: Part1.D5_PWM, R2.Pin_1
  N10: Part1.D6_PWM, R3.Pin_1
  N11: Part1.D7, R4.Pin_1, LED4.anode
  N12: Part1.5V, U1.P4, J2.pulse, S1.2, S2.2, S3.2, S4.2
  GND: Part1.GND, LED1.cathode, LED2.cathode, LED4.cathode, LED5.cathode, LED6.cathode, J1.pin1, U1.GND, J2.gnd, R18.Pin_0, R19.Pin_0, R20.Pin_0, R21.Pin_0
  N13: LED1.anode, R1.Pin_0
  N14: LED2.anode, R2.Pin_0
  N15: LED3.anode, R3.Pin_0
  N16: J1.pin2, R7.Pin_1
  N17: 7_Segment1.Segment_G, R15.Pin_1
  N18: 7_Segment1.Segment_F, R14.Pin_0
  N19: 7_Segment1.common_anode, R12.Pin_0, R13.Pin_0
  N20: 7_Segment1.Segment_E, R9.Pin_0
  N21: 7_Segment1.Segment_D, R8.Pin_0
  N22: 7_Segment1.Segment_DP, R10.Pin_0
  N23: 7_Segment1.Segment_C, R11.Pin_0
  N24: 7_Segment1.Segment_B, R17.Pin_0
  N25: 7_Segment1.Segment_A, R16.Pin_1
  N26: R8.Pin_1, U1.P0
  N27: R9.Pin_1, U1.A2
  N28: R10.Pin_1, U1.P2
  N29: R11.Pin_1, U1.SCL
  N30: R12.Pin_1, U1.A1
  N31: R13.Pin_1, U1.SDA
  N32: R14.Pin_1, U1.A0
  N33: R15.Pin_0, U1.P1
  N34: R16.Pin_0, U1.P3
  N35: U1.VCC, R17.Pin_1
  N36: S1.1, R18.Pin_1
  N37: S2.1, R19.Pin_1
  N38: S3.1, R20.Pin_1
  N39: S4.1, R21.Pin_1
